# Fritzing sketch fritzing_diagram (saved by Fritzing 0.9.3b)
breadboards: 1

parts:
  Arduino_MEGA = Arduino Mega 2560 (Rev3)
  Buffer_(LM741CN) = IC, DIP package, 8 pins [chip_label=IC]
  DAC0808 = IC, DIP package, 16 pins [chip_label=IC]
  External_Power_Supply_(Positive) = DC Power [voltage=5]
  R_REF+ = Resistor [tolerance=±5% resistance=5k package=THT]
  R_REF- = Resistor [tolerance=±5% resistance=5k package=THT]
  Compensation = Ceramic Capacitor [capacitance=0.1µF package="100 mil [THT, multilayer]"]
  Pos_or_Neg_Supply_Voltage = DC Power [voltage=15V]
  200 = Resistor [tolerance=±5% resistance=220 package="0603 [SMD]"]
  200_2 = Resistor [tolerance=±5% resistance=220 package="0603 [SMD]"]
  Lowpass_Cap_100uF = Capacitor Polarized [package=panasonic_e]
  Feedback_Buffer_(LM741CN)1 = IC, DIP package, 8 pins [chip_label=IC]

nets:
  N1: Arduino_MEGA.A0, Feedback_Buffer_(LM741CN)1.pin2, Feedback_Buffer_(LM741CN)1.pin6
  N2: Arduino_MEGA.GND, DAC0808.pin2, DAC0808.pin3, External_Power_Supply_(Positive).V-, R_REF-.Pin_1, Compensation.1, Pos_or_Neg_Supply_Voltage.V-, Lowpass_Cap_100uF.-
  N3: Arduino_MEGA.D22, DAC0808.pin12
  N4: Arduino_MEGA.D23, DAC0808.pin11
  N5: Arduino_MEGA.D24, DAC0808.pin10
  N6: Arduino_MEGA.D25, DAC0808.pin9
  N7: Arduino_MEGA.D26, DAC0808.pin8
  N8: Arduino_MEGA.D27, DAC0808.pin7
  N9: Arduino_MEGA.D28, DAC0808.pin6
  N10: Arduino_MEGA.D29, DAC0808.pin5
  N11: Buffer_(LM741CN).pin2, Buffer_(LM741CN).pin6, 200.Pin_0
  N12: Buffer_(LM741CN).pin3, DAC0808.pin4
  N13: Buffer_(LM741CN).pin4, Pos_or_Neg_Supply_Voltage.V+, Feedback_Buffer_(LM741CN)1.pin4
  N14: Buffer_(LM741CN).pin7, DAC0808.pin13, External_Power_Supply_(Positive).V+, R_REF+.Pin_1, Feedback_Buffer_(LM741CN)1.pin7
  N15: DAC0808.pin14, R_REF+.Pin_0
  N16: DAC0808.pin15, R_REF-.Pin_0
  N17: DAC0808.pin16, Compensation.0
  N18: 200.Pin_1, 200_2.Pin_0
  N19: 200_2.Pin_1, Lowpass_Cap_100uF.+, Feedback_Buffer_(LM741CN)1.pin3

notes:
  Vout
  Arduino 8 Bit PWM out
  parallel connection to DAC0808
  DAC0808 Output
